# Fritzing sketch mint_tin_hero_layout (saved by Fritzing 0.7.7b)
perfboards: 1

parts:
  U1 = atmega328 [package=dip]
  INPUT_SENSOR = Piezo Speaker
  J3 = female pin header, 8 pins [form="♀ (female)"]
  J4 = female pin header, 8 pins [form="♀ (female)"]
  R4 = Resistor [tolerance=±5% resistance=1M package=THT]
  SPKR1 = Loudspeaker
  R5 = Resistor [tolerance=±5% resistance=100 package=THT]
  S1 = Toggle Switch [package=THT]
  Part1 = LilyPad Coin Cell Battery Holder
  R6 = Resistor [tolerance=±5% resistance=100 package=THT]
  J5 = female pin header, 2 pins [form="♀ (female)"]
  J6 = female pin header, 2 pins [form="♀ (female)"]
  J7 = female pin header, 2 pins [form="♀ (female)"]
  LCD1 = LCD screen
  J8 = female pin header, 4 pins [form="♀ (female)"]
  R7 = Rotary Potentiometer (Small) [maximum_resistance=10kΩ]

nets:
  N1: U1.RESET, J7.pin1
  N2: U1.D0_(RX), J6.pin1
  N3: U1.D1_(TX), J5.pin1
  N4: U1.D2, R6.Pin_0
  N5: U1.D3_(PWM), J3.pin2, LCD1.RS
  N6: U1.D4, J3.pin3, LCD1.E
  VCC: U1.VCC, U1.AVCC, J3.pin1, S1.COM, J5.pin2, LCD1.VDD, R7.leg1
  GND: U1.GND, INPUT_SENSOR.pin1, J3.pin8, J4.pin1, J4.pin3, R4.Pin_1, R5.Pin_0, Part1.-, LCD1.VSS, LCD1.R/W, LCD1.LED-, R7.leg2
  N7: U1.D5_(PWM), J4.pin6, LCD1.DB4
  N8: U1.D6_(PWM), J3.pin6, LCD1.DB5
  N9: U1.D7, J4.pin7, LCD1.DB6
  N10: U1.D8, J3.pin7, LCD1.DB7
  N11: U1.D9_(PWM), SPKR1.pin2
  N12: U1.D10_(PWM), J8.pin1
  N13: U1.D11_(PWM), J8.pin2
  N14: U1.D12, J8.pin3
  N15: U1.D13, J8.pin4
  N16: U1.A0, INPUT_SENSOR.pin2, R4.Pin_0
  N17: J4.pin2, LCD1.V0, R7.wiper
  N18: J4.pin8, R6.Pin_1, LCD1.LED+
  N19: SPKR1.pin1, R5.Pin_1
  N20: S1.L1, Part1.+

notes:
  CR2016
  x2
  Header:
  TX VCC
  RX ---
  RES GND
